# Fritzing sketch zspod (saved by Fritzing 0.9.9b)
circuit board: 7.6301cm x 6.08316cm
breadboards: 1

parts:
  M+ = Momentary Switch [package=ksa_sealed_tac_switch]
  M- = Momentary Switch [package=ksa_sealed_tac_switch]
  Y+ = Momentary Switch [package=ksa_sealed_tac_switch]
  Y- = Momentary Switch [package=ksa_sealed_tac_switch]
  D+ = Momentary Switch [package=ksa_sealed_tac_switch]
  D- = Momentary Switch [package=ksa_sealed_tac_switch]
  m- = Momentary Switch [package=ksa_sealed_tac_switch]
  h+ = Momentary Switch [package=ksa_sealed_tac_switch]
  h- = Momentary Switch [package=ksa_sealed_tac_switch]
  Arduino = Arduino Nano (Rev3.0)
  D23 = Diode [package=sma-diode]
  D28 = Diode [package=sma-diode]
  D22 = Diode [package=sma-diode]
  D24 = Diode [package=sma-diode]
  D25 = Diode [package=sma-diode]
  D26 = Diode [package=sma-diode]
  D27 = Diode [package=sma-diode]
  D29 = Diode [package=sma-diode]
  D30 = Diode [package=sma-diode]
  m+ = Momentary Switch [package=ksa_sealed_tac_switch]
  RTC = Real Time Clock Module - DS1307 RTC Breakout Board from Amazon
  R2 = Resistor [tolerance=±5% resistance=100 package="0402 [SMD]"]
  R1 = Resistor [tolerance=±5% resistance=100 package="0402 [SMD]"]
  R4 = Resistor [tolerance=±5% resistance=100 package="0402 [SMD]"]
  R5 = Resistor [tolerance=±5% resistance=100 package="0402 [SMD]"]
  R6 = Resistor [tolerance=±5% resistance=100 package="0402 [SMD]"]
  R7 = Resistor [tolerance=±5% resistance=100 package="0402 [SMD]"]
  R8 = Resistor [tolerance=±5% resistance=100 package="0402 [SMD]"]
  R9 = Resistor [tolerance=±5% resistance=100 package="0402 [SMD]"]
  R10 = Resistor [tolerance=±5% resistance=100 package="0402 [SMD]"]
  R11 = Resistor [tolerance=±5% resistance=100 package="0402 [SMD]"]
  D31 = Diode [package=sma-diode]
  RST = Momentary Switch [package=ksa_sealed_tac_switch]
  BAT = mystery part, 2 pins [chip_label=?]
  R12 = Resistor [tolerance=±5% resistance=100 package="0402 [SMD]"]
  EPD = EPD connector [package=sod-323]

nets:
  N1: M+.1, M+.2, Arduino.A2, D24.A, R4.Pin_0
  VCC: M+.3, M+.4, M-.3, M-.4, Y+.3, Y+.4, Y-.3, Y-.4, D+.3, D+.4, D-.3, D-.4, m-.3, m-.4, h+.3, h+.4, h-.3, h-.4, Arduino.5V, m+.3, m+.4, RTC.VCC, BAT.pin1, EPD.VCC
  N2: M-.1, M-.2, Arduino.A3, D25.A, R5.Pin_0
  N3: Y+.1, Y+.2, Arduino.A0, D22.A, R1.Pin_0
  N4: Y-.1, Y-.2, Arduino.A1, D23.A, R2.Pin_0
  N5: D+.1, D+.2, Arduino.A6, D26.A, R6.Pin_0
  N6: D-.1, D-.2, Arduino.A7, D27.A, R7.Pin_0
  N7: m-.1, m-.2, Arduino.D5, D29.A, R9.Pin_0
  N8: h+.1, h+.2, Arduino.D4, D30.A, R10.Pin_0
  N9: h-.1, h-.2, Arduino.D3, R11.Pin_0, D31.A
  N10: Arduino.RESET, RST.1
  GND: Arduino.GND, RTC.GND, R2.Pin_1, R1.Pin_1, R4.Pin_1, R5.Pin_1, R6.Pin_1, R7.Pin_1, R8.Pin_1, R9.Pin_1, R10.Pin_1, R11.Pin_1, RST.3, BAT.pin2, R12.Pin_1, EPD.GND
  N11: Arduino.D2, D23.C, D28.C, D22.C, D24.C, D25.C, D26.C, D27.C, D29.C, D30.C, D31.C, R12.Pin_0
  N12: Arduino.D6, D28.A, m+.1, m+.2, R8.Pin_0
  N13: Arduino.D7, EPD.BUSY
  N14: Arduino.D8, EPD.RST
  N15: Arduino.D9, EPD.DC
  N16: Arduino.D10, EPD.CS
  N17: Arduino.D11/MOSI, EPD.DIN
  N18: Arduino.A5, RTC.SCL
  N19: Arduino.A4, RTC.SDA
  N20: Arduino.D13/SCK, EPD.CLK

notes:
  +
  -
  zspod
  h
  m
  D
  M
  Y
  RST

custom parts:
  Real Time Clock Module - DS1307 RTC Breakout Board from Amazon: This a custom designed module for the DS1307 Real Time Clock. The module comes fully assembled and pre-programmed with the current time (ok, so it's our current time - MST). The included Lithium coin cell battery (CR1225 41mAh) will run the module for a minimum of 9 years (17 years typical) without external 5V power. The DS1307 is accessed via the I2C protocol. We've written a test-bed to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

// code stored in the sketch: zspod.ino
#include <Wire.h>
#include <RTClib.h>
#include <avr/sleep.h>
#include <avr/power.h>

#include <SPI.h>
#include "epd4in2.h"
#include "epdpaint.h"

#include "buttons.h"
#include "trans.h"
#include "timing.h"
#include "globals.h"

#define COLORED     0
#define UNCOLORED   1

#define TOPBAR_HEIGHT 30
#define BIGSTRING_MARGIN 5
#define BIGSTRING_SINGLE_Y ((300 - TOPBAR_HEIGHT - FONT60_HEIGHT) / 2  + TOPBAR_HEIGHT)
#define BIGSTRING_DOUBLE_Y_UPPER ((300 - TOPBAR_HEIGHT - (FONT60_HEIGHT * 2) - BIGSTRING_MARGIN ) / 2 + TOPBAR_HEIGHT)
#define BIGSTRING_DOUBLE_Y_LOWER (BIGSTRING_DOUBLE_Y_UPPER + FONT60_HEIGHT + BIGSTRING_MARGIN)
 
#define SMALLSTRING_X (400 - 17 * 5) / 2
#define SMALLSTRING_Y (300 - TOPBAR_HEIGHT - 24) / 2 + TOPBAR_HEIGHT


unsigned char image[750];
Paint paint(image, 200, 30);
Epd epd;

char text_1[20] = {0};
char text_2[20] = {0};

void setup() {
  // RTC and serial
  Serial.begin(9600);
  rtc.begin();

  DateTime now = rtc.now();
  Serial.print("Start time: ");
  char dt_format[] = DATE_TIME_FORMAT;
  Serial.println(now.toString(dt_format));

  // buttons
  init_buttons();

  // display
  updateDisplay();
  
  // Timing
  Timer::init_timer();
  delay(100); 
}


void loop() {
  int secs_to_sleep = time_change_mode ? 5 : secsToSleep();
  time_change_mode = false;
  Timer::start_timer(secs_to_sleep);
  Timer::do_sleep();
  updateDisplay();
}

void  updateDisplay() {
  
  DateTime now = rtc.now();
  //now = DateTime(2021, 12, 12, 11, 29, 0);

  char dateTemplate[] = ", DD.MM.YYYY";
  char date[30];
  const char* weekday = Trans::weekdays[now.dayOfTheWeek()];
  strcpy(date, weekday);
  strcpy(date + strlen(weekday), now.toString(dateTemplate));

  char timecode[6];
  char t_format[] = TIME_FORMAT;
  strcpy(timecode, now.toString(t_format));

  char dt_format[] = DATE_TIME_FORMAT;
  Serial.print("Refresh Time: ");
  Serial.println(now.toString(dt_format));

  // (400 - strlen(date)* fontwidth) / 2
  int fromLeft = 200 - (strlen(date) * 17) / 2;

  epd.Init();
  epd.ClearFrameHidden();

  paint.SetHeight(TOPBAR_HEIGHT);
  paint.SetWidth(200);
  paint.Clear(UNCOLORED);
  paint.DrawFilledRectangle(0,0, 200, TOPBAR_HEIGHT, COLORED);
  paint.DrawStringAt(fromLeft, 5, date, &Font24, UNCOLORED);
  paint.DrawStringAt(100, 100, timecode, &Font24, COLORED);
  epd.SetPartialWindow(paint.GetImage(), 0, 0, paint.GetWidth(), paint.GetHeight());
  
  paint.Clear(UNCOLORED);
  paint.DrawFilledRectangle(0, 0, 200, TOPBAR_HEIGHT, COLORED);
  paint.DrawStringAt(fromLeft - 200, 5, date, &Font24, UNCOLORED);
  epd.SetPartialWindow(paint.GetImage(), 200, 0, paint.GetWidth(), paint.GetHeight());


  if (!time_change_mode) {
    Trans::upperString(now, text_1);
    Trans::lowerString(now, text_2);
  
    int width_upper = paint.BigStringWidth(text_1, font60);
    int width_lower = paint.BigStringWidth(text_2, font60);
  
    int from_left_upper = 200 - width_upper / 2;
    int from_left_lower = 200 - width_lower / 2;
    
    paint.DrawBigStringAt(from_left_upper, BIGSTRING_DOUBLE_Y_UPPER, text_1, font60, COLORED, epd);
    paint.DrawBigStringAt(from_left_lower, width_upper ? BIGSTRING_DOUBLE_Y_LOWER : BIGSTRING_SINGLE_Y, text_2, font60, COLORED, epd);
  }
  else {
    paint.Clear(UNCOLORED);
    paint.DrawStringAt(0, 0, timecode, &Font24, COLORED);
    epd.SetPartialWindow(paint.GetImage(), SMALLSTRING_X, SMALLSTRING_Y, paint.GetWidth(), paint.GetHeight());
  }

  epd.DisplayFrame();
  epd.Sleep();

  // wait for flush
  delay(50);
}

int secsToSleep() {
  DateTime now = rtc.now();
  
  uint8_t mins = now.minute();
  int next_wakeup_mins = Trans::roundTo(mins, 5) + 3;

  int secs_til_wake = (next_wakeup_mins - mins) * 60 - now.second() + 3;

  return secs_til_wake;
}
